// Logisim project 502044_N14T02_52100841_NguyenTanThahnh_tuan4.circ as structural Verilog: 1 circuit, main circuit main
module main (
);

  wire button_1_out, clock_1_out, clock_2_out, clock_3_out;
  wire [2:0] counter_1_q, rom_2_data;
  wire [3:0] counter_3_q, rom_1_data;
  wire [4:0] counter_2_q;
  wire [6:0] rom_3_data;

  Clock clock_1 (.out(clock_1_out));
  Clock clock_2 (.out(clock_2_out));
  Clock clock_3 (.out(clock_3_out));
  Counter #(.width(3), .max('h7)) counter_1 (
    .count(clock_2_out), .Q(counter_1_q), .clk(clock_2_out));  // open: load, D, carry, clr
  Counter #(.width(5), .max('h1f)) counter_2 (
    .Q(counter_2_q), .clk(clock_3_out), .clr(button_1_out));  // open: load, D, count, carry
  Button button_1 (.out(button_1_out));
  Counter #(.width(4), .max('hf)) counter_3 (
    .count(clock_1_out), .Q(counter_3_q), .clk(clock_1_out));  // open: load, D, carry, clr
  ROM #(.addrWidth(4), .dataWidth(4)) rom_1 (.addr(counter_3_q), .data(rom_1_data));  // open: sel
  ROM #(.addrWidth(3), .dataWidth(3)) rom_2 (.addr(counter_1_q), .data(rom_2_data));  // open: sel
  ROM #(.addrWidth(5), .dataWidth(7)) rom_3 (.addr(counter_2_q), .data(rom_3_data));  // open: sel
  TTY tty_1 (.data(rom_3_data), .clk(clock_3_out), .clr(button_1_out));  // open: we
  Hex_Digit_Display hex_digit_display_1 (.value(rom_1_data));  // open: dp
  LED led_1 (.in(rom_2_data[2]));
  LED led_2 (.in(rom_2_data[1]));
  LED led_3 (.in(rom_2_data[0]));

  // Notes on the sheet:
  //   clock
  //   clock
  //   clock
  //   counter
  //   counter
  //   counter
  //   bottom
  //   ROM
  //   ROM
  //   ROM
  //   contents of rom_1 (hex, n*v repeats v):
  //   0 1 2 3 4 5 6 7 8 9 a b c d e f
  //   contents of rom_2 (hex, n*v repeats v):
  //   2 4*1 4 4 2
  //   contents of rom_3 (hex, n*v repeats v):
  //   61 63 20 62 61 6e 20 68 6f 63 20 74 6f 74 21 20 0 0 21 31 0 5 2 6 3 6 4 2 21 4 24 23
  //   hex display
  //   TTY
  //   đèn dỏ
  //   đèn vàng
  //   đèn xanh
endmodule
