// Logisim project Lab1.2_CircuitF3.circ as structural Verilog: 1 circuit, main circuit main
module main (
  input  x,
  input  y,
  input  z,
  input  in_4,
  input  x_2,
  input  y_2,
  input  B,
  input  C,
  input  x_3,
  input  x_4,
  input  y_3,
  input  y_4,
  input  w,
  input  z_2,
  input  z_3,
  input  A,
  input  a_2,
  input  B_2,
  input  b_3,
  input  C_2,
  input  c_3,
  input  D,
  output out_23,
  output out_24,
  output out_25,
  output out_26,
  output out_27,
  output out_28,
  output out_29
);

  wire and_1_out, and_2_out, and_3_out, and_4_out, and_5_out, and_6_out, and_7_out, and_8_out, and_9_out,
       and_10_out, and_11_out, and_13_out, and_14_out, and_16_out, and_17_out, not_1_out, not_2_out,
       not_3_out, not_4_out, not_5_out, or_1_out, or_2_out, or_6_out, or_7_out, or_8_out, or_9_out, or_10_out;

  not not_1 (not_1_out, y);
  not not_2 (not_2_out, x);
  not not_3 (not_3_out, C);
  and and_1 (and_1_out, x_4, x_4, y_4, z_2);
  and and_2 (and_2_out, x_4, z_2);
  and and_3 (and_3_out, B_2, C_2);
  and and_4 (and_4_out, A, D);
  and and_5 (and_5_out, A, B_2);
  and and_6 (and_6_out, C_2, D);
  and and_7 (and_7_out, x, not_1_out);
  and and_8 (and_8_out, not_2_out, z, z);
  and and_9 (and_9_out, in_4, B, C);
  and and_10 (and_10_out, in_4, B);
  and and_11 (and_11_out, in_4, B, not_3_out);
  or or_1 (or_1_out, and_3_out, and_4_out);
  or or_2 (or_2_out, and_5_out, and_6_out);
  or or_3 (out_23, and_7_out, and_8_out);
  or or_4 (out_26, and_1_out, and_2_out);
  or or_5 (out_25, and_9_out, and_10_out, and_11_out);
  and and_12 (out_29, or_1_out, or_2_out);
  not not_4 (not_4_out, z_3);
  not not_5 (not_5_out, y_2);
  and and_13 (and_13_out, w, z_3);
  and and_14 (and_14_out, w, not_4_out);
  or or_6 (or_6_out, c_3, a_2);
  or or_7 (or_7_out, a_2, b_3, c_3);
  or or_8 (or_8_out, x_2, y_2);
  or or_9 (or_9_out, x_2, not_5_out);
  or or_10 (or_10_out, and_13_out, and_14_out);
  and and_15 (out_24, or_8_out, or_9_out);
  and and_16 (and_16_out, x_3, y_3);
  buf and_17 (and_17_out, or_10_out);  // AND_Gate
  and and_18 (out_28, or_6_out, or_7_out);
  or or_11 (out_27, and_16_out, and_17_out);

  // Notes on the sheet:
  //   F3 = xy' + x'z
  //   a) ABC + AB + ABC'
  //   A
  //   b) xyz + xz
  //   e
  //   YÊU CẦU 3
  //   E) (BC+AD)(AB+CD)
  //   xy'
  //   x'z
  //   ABC
  //   AB
  //   ABC'
  //   xyz
  //   xz
  //   BC
  //   AD
  //   AB
  //   CD
  //   (BC+AD)
  //   (AB+CD)
  //   F3
  //   d) xy + x(wz+wz')
  //   f) (a+c)(a+b+c)
  //   c) (x+y)(x+y')
  //   wz
  //   wz'
  //   (x+y)
  //   (x+y')
  //   (wz+wz')
  //   (a+c)
  //   (a+b+c)
  //   xy
  //   x(wz+wz')
endmodule
