// Logisim project lab1.1_MyFirstCircuite.circ as structural Verilog: 1 circuit, main circuit main
module main (
  input  A,
  input  B,
  output out_3
);

  wire and_1_out, and_2_out, not_1_out, not_2_out;

  not not_1 (not_1_out, A);
  not not_2 (not_2_out, B);
  and and_1 (and_1_out, not_1_out, B);
  and and_2 (and_2_out, not_2_out, A);
  or or_1 (out_3, and_1_out, and_2_out);

  // Notes on the sheet:
  //   Monday, October 25, 2021
  //   XOR circuit
endmodule
