// Logisim project Lab2_1.circ as structural Verilog: 4 circuits, main circuit main
module main (
  input  A,
  input  B,
  input  A_2,
  input  B_2,
  input  CIN
);

  wire full_adder_1_cout, full_adder_1_s, half_adder_1_cout, half_adder_1_s;

  HALF_ADDER half_adder_1 (.A(A), .B(B), .S(half_adder_1_s), .COUT(half_adder_1_cout));
  LED led_1 (.in(half_adder_1_s));
  LED led_2 (.in(half_adder_1_cout));
  FULL_ADDER full_adder_1 (.A(A_2), .B(CIN), .CIN(B_2), .S(full_adder_1_s), .COUT(full_adder_1_cout));
  LED led_3 (.in(full_adder_1_cout));
  LED led_4 (.in(full_adder_1_s));

  // Notes on the sheet:
  //   COUT
  //   S
  //   COUT
  //   S
endmodule

module HALF_ADDER (
  input  A,
  input  B,
  output S,
  output COUT
);

  and and_1 (COUT, A, B);
  xor xor_1 (S, A, B);

  // Notes on the sheet:
  //   HALF ADDER
endmodule

module FULL_ADDER (
  input  A,
  input  B,
  input  CIN,
  output S,
  output COUT
);

  wire and_1_out, and_2_out, and_3_out, xor_1_out;

  and and_1 (and_1_out, CIN, A);
  and and_2 (and_2_out, CIN, B);
  and and_3 (and_3_out, B, A);
  xor xor_1 (xor_1_out, A, B);
  xor xor_2 (S, xor_1_out, CIN);
  or or_1 (COUT, and_1_out, and_2_out, and_3_out);

  // Notes on the sheet:
  //   FULL ADDER
endmodule

module full_adder_2 (
  input  A,
  input  B,
  input  C,
  output S,
  output COUT
);

  wire half_adder_1_cout, half_adder_1_s, half_adder_2_cout;

  HALF_ADDER half_adder_1 (.A(A), .B(B), .S(half_adder_1_s), .COUT(half_adder_1_cout));
  HALF_ADDER half_adder_2 (.A(half_adder_1_s), .B(C), .S(S), .COUT(half_adder_2_cout));
  or or_1 (COUT, half_adder_2_cout, half_adder_1_cout);
endmodule
