// Logisim project Lab2_2.circ as structural Verilog: 3 circuits, main circuit main
module main (
  input  [3:0] A_4,
  input  [3:0] B_4,
  input  Cin,
  output Cout,
  output [3:0] S
);

  wire [3:0] not_1_out;

  Hex_Digit_Display hex_digit_display_1 (.value(A_4));  // open: dp
  Hex_Digit_Display hex_digit_display_2 (.value(B_4));  // open: dp
  assign not_1_out = ~B_4;  // NOT_Gate not_1, 4 bits wide
  _4_bit_adder u_4_bit_adder_1 (.A_4(A_4), .B_4(not_1_out), .Cin(Cin), .Cout(Cout), .s_4(S));
  Hex_Digit_Display hex_digit_display_3 (.value(S));  // open: dp
endmodule

module FULLADDER (
  input  A,
  input  B,
  input  Cin,
  output S,
  output Cout
);

  wire and_1_out, and_2_out, and_3_out, and_4_out, and_5_out, and_6_out, and_7_out, not_1_out, not_2_out,
       not_3_out, not_4_out, not_5_out, not_6_out;

  and and_1 (and_1_out, B, Cin);
  and and_2 (and_2_out, A, Cin);
  and and_3 (and_3_out, A, B);
  not not_1 (not_1_out, A);
  not not_2 (not_2_out, B);
  not not_3 (not_3_out, A);
  not not_4 (not_4_out, Cin);
  not not_5 (not_5_out, B);
  not not_6 (not_6_out, Cin);
  or or_1 (S, and_1_out, and_2_out, and_3_out);
  and and_4 (and_4_out, not_1_out, not_2_out, Cin);
  and and_5 (and_5_out, not_3_out, B, not_4_out);
  and and_6 (and_6_out, A, not_5_out, not_6_out);
  and and_7 (and_7_out, A, B, Cin);
  or or_2 (Cout, and_4_out, and_5_out, and_6_out, and_7_out);
endmodule

module _4_bit_adder (
  input  [3:0] A_4,
  input  [3:0] B_4,
  input  Cin,
  output Cout,
  output [3:0] s_4
);

  wire fulladder_1_cout, fulladder_2_cout, fulladder_3_cout;

  Hex_Digit_Display hex_digit_display_1 (.value(A_4));  // open: dp
  FULLADDER fulladder_1 (.A(A_4[0]), .B(B_4[0]), .Cin(Cin), .S(s_4[0]), .Cout(fulladder_1_cout));
  Hex_Digit_Display hex_digit_display_2 (.value(B_4));  // open: dp
  FULLADDER fulladder_2 (.A(A_4[1]), .B(B_4[1]), .Cin(fulladder_1_cout), .S(s_4[1]), .Cout(fulladder_2_cout));
  FULLADDER fulladder_3 (.A(A_4[2]), .B(B_4[2]), .Cin(fulladder_2_cout), .S(s_4[2]), .Cout(fulladder_3_cout));
  Hex_Digit_Display hex_digit_display_3 (.value(s_4));  // open: dp
  FULLADDER fulladder_4 (.A(A_4[3]), .B(B_4[3]), .Cin(fulladder_3_cout), .S(s_4[3]), .Cout(Cout));
endmodule
